# Fritzing sketch KeyInputBoard (saved by Fritzing 0.9.4)
breadboards: 1

parts:
  부품1 = Arduino Uno (Rev3)
  S1 = Pushbutton [package="[THT]"]
  S2 = Pushbutton [package="[THT]"]

nets:
  N1: 부품1.GND, S1.Pin_3, S1.Pin_4, S2.Pin_3, S2.Pin_4
  N2: 부품1.D2, S2.Pin_1, S2.Pin_2
  N3: 부품1.D3_PWM, S1.Pin_2
